# Fritzing sketch 2004A LCD display with Arduino Mega (saved by Fritzing 0.8.7b)

parts:
  Part1 = Arduino Mega 2560 (Rev3)
  LCD2004-I2C1 = LCD2004-I2C

nets:
  N1: Part1.D21/SCL, LCD2004-I2C1.SCL
  N2: Part1.D20/SDA, LCD2004-I2C1.SDA
  5V: Part1.5V, LCD2004-I2C1.VCC
  GND: Part1.GND, LCD2004-I2C1.GND

custom parts:
  LCD2004-I2C: A standard character display with 4x20 characters. Comes in many colors with LCM2004 IIC attached.
